// Logisim project comparator-circuit.circ as structural Verilog: 21 circuits, main circuit main
module main (
  input  [7:0] INPR
);

  wire alu_1_e_out, Clock, clock_1_out, E, FGI, FGO, HLT, I, IEN, mr_controler_1_mr_ld, not_1_out, not_2_out,
       p, pc_controler_1_clear, pc_controler_1_inc, pc_controler_1_load, R, r_t;
  wire [2:0] BUS_Selector;
  wire [3:0] outr_1_out_5, outr_1_out_6;
  wire [7:0] D;
  wire [11:0] B;
  wire [15:0] AC, alu_1_out, AR, BUS_IN, DR, IR, MR, PC, ram_1_data, T, TR;

  AR ar_1 (.Bus_IN(BUS_IN), .I(I), .R(R), .Clock(Clock), .T(T), .D(D), .Bus_OUT(AR));
  IR ir_1 (.T(T), .B(B), .I(I), .D(D), .Bus_OUT(IR), .HLT(HLT), .Clock(Clock), .R(R), .Bus_IN(BUS_IN));
  PC pc_1 (
    .Bus_IN(BUS_IN), .Load(pc_controler_1_load), .INC(pc_controler_1_inc), .Clock(Clock),
    .Clear(pc_controler_1_clear), .Bus_OUT(PC));
  PC_Controler pc_controler_1 (
    .DR(DR), .AC(AC), .B(B), .D(D), .R(R), .FGI(FGI), .FGO(FGO), .E(E), .T(T), .r_2(r_t), .p(p),
    .Load(pc_controler_1_load), .Clear(pc_controler_1_clear), .INC(pc_controler_1_inc));
  SC sc_1 (.R(R), .I(I), .T(T), .D(D), .Clock(Clock), .T_2(T));
  BUS_Controler bus_controler_1 (.D(D), .T(T), .B(B), .R(R), .I(I), .p(p), .BUS(BUS_Selector));
  TR tr_1 (.Bus_IN(BUS_IN), .T(T), .R(R), .Bus_OUT(TR), .Clock(Clock));
  IEN ien_1 (.R(R), .p(p), .B(B), .Clock(Clock), .T(T), .OUT(IEN));
  FGI fgi_1 (.p(p), .B(B), .Clock(Clock), .OUT(FGI));
  FGO fgo_1 (.p(p), .B(B), .Clock(Clock), .OUT(FGO));
  R r_1 (.IEN(IEN), .FGO(FGO), .FGI(FGI), .Clock(Clock), .T(T), .OUT(R));
  Clock clock_1 (.out(clock_1_out));
  not not_1 (not_1_out, HLT);
  DR dr_1 (.Bus_IN(BUS_IN), .D(D), .T(T), .Clock(Clock), .Bus_OUT(DR));
  OUTR outr_1 (.Bus_IN(BUS_IN), .P(p), .B(B), .out_5(outr_1_out_5), .out_6(outr_1_out_6), .Clock(Clock));
  and and_1 (Clock, clock_1_out, not_1_out);
  Hex_Digit_Display hex_digit_display_1 (.value(outr_1_out_5));  // open: dp
  Hex_Digit_Display hex_digit_display_2 (.value(outr_1_out_6));  // open: dp
  and and_2 (r_t, D[7], ~I, T[3]);  // AND_Gate
  MR_Controler mr_controler_1 (.D(D), .T(T), .R(R), .MR_LD(mr_controler_1_mr_ld));
  and and_3 (p, D[7], I, T[3]);
  ALU alu_1 (
    .r(r_t), .E(E), .p(p), .E_OUT(alu_1_e_out), .AC(AC), .DR(DR), .INPR(INPR), .D(D), .T(T), .B(B),
    .OUT(alu_1_out));
  RAM #(.addrWidth(12), .dataWidth(16)) ram_1 (
    .addr(AR[11:0]), .data(ram_1_data), .clk(Clock), .ld(mr_controler_1_mr_ld));  // open: sel, clr
  not not_2 (not_2_out, mr_controler_1_mr_ld);
  assign ram_1_data = not_2_out ? BUS_IN : 16'bz;  // Controlled_Buffer controlled_buffer_1
  AC ac_1 (.ALU_IN(alu_1_out), .r(r_t), .B(B), .Clock(Clock), .Bus_OUT(AC));
  assign MR = mr_controler_1_mr_ld ? ram_1_data : 16'bz;  // Controlled_Buffer controlled_buffer_2
  E e_1 (.Clock(Clock), .r(r_t), .B(B), .D(D), .IN(alu_1_e_out), .T(T), .E_Out(E));
  Multiplexer #(.select(3), .width(16), .enable("false")) multiplexer_1 (
    .in1(PC), .in2(TR), .in3(IR), .in4(AC), .in5(AR), .in6(DR), .in7(MR), .out(BUS_IN), .sel(BUS_Selector));  // open: in0
endmodule

module AR (
  input  [15:0] Bus_IN,
  input  I,
  input  R,
  input  Clock,
  input  [15:0] T,
  input  [7:0] D,
  output [15:0] Bus_OUT
);

  wire and_1_out, and_2_out, and_3_out, and_4_out, and_5_out, not_1_out, not_2_out, or_1_out, or_2_out;
  wire [11:0] INC_s, multiplexer_1_out;
  wire [15:12] INC_s_2;

  not not_1 (not_1_out, D[7]);
  not not_2 (not_2_out, R);
  and and_1 (and_1_out, not_1_out, I, T[3]);
  and and_2 (and_2_out, T[2], not_2_out);
  and and_3 (and_3_out, not_2_out, T[0]);
  and and_4 (and_4_out, D[5], T[4]);
  and and_5 (and_5_out, R, T[0]);
  or or_1 (or_1_out, and_1_out, and_2_out, and_3_out);
  Multiplexer #(.width(12), .enable("false")) multiplexer_1 (
    .in0(INC_s), .in1(Bus_IN[11:0]), .out(multiplexer_1_out), .sel(or_1_out));
  or or_2 (or_2_out, or_1_out, and_4_out);
  Adder_16 INC (.A({4'b0000, Bus_OUT[11:0]}), .B(16'h1), .Cin(1'b0), .S({INC_s_2, INC_s}));  // open: Cout
  Register #(.width(12)) AR (.D(multiplexer_1_out), .en(or_2_out), .Q(Bus_OUT[11:0]), .clk(Clock), .clr(and_5_out));

  assign Bus_OUT[15:12] = 4'b0000;
endmodule

module Full_Adder (
  input  Ci,
  input  Ai,
  input  Bi,
  output Si,
  output Ci_1
);

  wire half_adder_1_c, half_adder_1_s, half_adder_2_c;

  Half_Adder half_adder_1 (.A(Ai), .B(Bi), .S(half_adder_1_s), .C(half_adder_1_c));
  Half_Adder half_adder_2 (.A(Ci), .B(half_adder_1_s), .S(Si), .C(half_adder_2_c));
  or or_1 (Ci_1, half_adder_2_c, half_adder_1_c);
endmodule

module Adder_16 (
  input  [15:0] A,
  input  [15:0] B,
  input  Cin,
  output [15:0] S,
  output Cout
);

  wire full_adder_2_ci_1, full_adder_3_ci_1, full_adder_4_ci_1, full_adder_5_ci_1, full_adder_6_ci_1,
       full_adder_7_ci_1, full_adder_8_ci_1, full_adder_9_ci_1, full_adder_10_ci_1, full_adder_11_ci_1,
       full_adder_12_ci_1, full_adder_13_ci_1, full_adder_14_ci_1, full_adder_15_ci_1, full_adder_16_ci_1;

  Full_Adder full_adder_1 (.Ci(full_adder_2_ci_1), .Ai(A[15]), .Bi(B[15]), .Si(S[15]), .Ci_1(Cout));
  Full_Adder full_adder_2 (.Ci(full_adder_3_ci_1), .Ai(A[14]), .Bi(B[14]), .Si(S[14]), .Ci_1(full_adder_2_ci_1));
  Full_Adder full_adder_3 (.Ci(full_adder_4_ci_1), .Ai(A[13]), .Bi(B[13]), .Si(S[13]), .Ci_1(full_adder_3_ci_1));
  Full_Adder full_adder_4 (.Ci(full_adder_5_ci_1), .Ai(A[12]), .Bi(B[12]), .Si(S[12]), .Ci_1(full_adder_4_ci_1));
  Full_Adder full_adder_5 (.Ci(full_adder_6_ci_1), .Ai(A[11]), .Bi(B[11]), .Si(S[11]), .Ci_1(full_adder_5_ci_1));
  Full_Adder full_adder_6 (.Ci(full_adder_7_ci_1), .Ai(A[10]), .Bi(B[10]), .Si(S[10]), .Ci_1(full_adder_6_ci_1));
  Full_Adder full_adder_7 (.Ci(full_adder_8_ci_1), .Ai(A[9]), .Bi(B[9]), .Si(S[9]), .Ci_1(full_adder_7_ci_1));
  Full_Adder full_adder_8 (.Ci(full_adder_9_ci_1), .Ai(A[8]), .Bi(B[8]), .Si(S[8]), .Ci_1(full_adder_8_ci_1));
  Full_Adder full_adder_9 (.Ci(full_adder_10_ci_1), .Ai(A[7]), .Bi(B[7]), .Si(S[7]), .Ci_1(full_adder_9_ci_1));
  Full_Adder full_adder_10 (.Ci(full_adder_11_ci_1), .Ai(A[6]), .Bi(B[6]), .Si(S[6]), .Ci_1(full_adder_10_ci_1));
  Full_Adder full_adder_11 (.Ci(full_adder_12_ci_1), .Ai(A[5]), .Bi(B[5]), .Si(S[5]), .Ci_1(full_adder_11_ci_1));
  Full_Adder full_adder_12 (.Ci(full_adder_13_ci_1), .Ai(A[4]), .Bi(B[4]), .Si(S[4]), .Ci_1(full_adder_12_ci_1));
  Full_Adder full_adder_13 (.Ci(full_adder_14_ci_1), .Ai(A[3]), .Bi(B[3]), .Si(S[3]), .Ci_1(full_adder_13_ci_1));
  Full_Adder full_adder_14 (.Ci(full_adder_15_ci_1), .Ai(A[2]), .Bi(B[2]), .Si(S[2]), .Ci_1(full_adder_14_ci_1));
  Full_Adder full_adder_15 (.Ci(full_adder_16_ci_1), .Ai(A[1]), .Bi(B[1]), .Si(S[1]), .Ci_1(full_adder_15_ci_1));
  Full_Adder full_adder_16 (.Ci(Cin), .Ai(A[0]), .Bi(B[0]), .Si(S[0]), .Ci_1(full_adder_16_ci_1));
endmodule

module Half_Adder (
  input  A,
  input  B,
  output S,
  output C
);

  xor xor_1 (S, A, B);
  and and_1 (C, A, B);
endmodule

module IR (
  input  [15:0] T,
  input  Clock,
  input  R,
  input  [15:0] Bus_IN,
  output [11:0] B,
  output I,
  output [7:0] D,
  output [15:0] Bus_OUT,
  output HLT
);

  wire and_1_out, not_1_out;

  not not_1 (not_1_out, R);
  and and_1 (and_1_out, not_1_out, T[1]);
  Register #(.width(16)) register_1 (.D(Bus_IN), .en(and_1_out), .Q({Bus_OUT[15:12], B}), .clk(Clock));  // open: clr
  and and_2 (HLT, B[0], ~B[1], ~B[2], ~B[3], ~B[4], ~B[5], ~B[6], ~B[7], ~B[8], ~B[9], ~B[10], ~B[11], Bus_OUT[12], Bus_OUT[13], Bus_OUT[14], ~Bus_OUT[15]);  // AND_Gate
  Decoder #(.select(3), .enable("false")) decoder_1 (
    .out0(D[0]), .out1(D[1]), .out2(D[2]), .out3(D[3]), .out4(D[4]), .out5(D[5]), .out6(D[6]), .out7(D[7]),
    .sel(Bus_OUT[14:12]));

  assign Bus_OUT[11:0] = B;
  assign I = Bus_OUT[15];
endmodule

module PC (
  input  [15:0] Bus_IN,
  input  Clear,
  input  Load,
  input  INC,
  input  Clock,
  output [15:0] Bus_OUT
);

  wire or_1_out;
  wire [11:0] adder_1_out, multiplexer_1_out;
  wire [15:0] INC_s;

  or or_1 (or_1_out, Load, INC);
  Multiplexer #(.width(12), .enable("false")) multiplexer_1 (
    .in0(adder_1_out), .in1(Bus_IN[11:0]), .out(multiplexer_1_out), .sel(Load));
  Adder #(.width(12)) adder_1 (.a(Bus_OUT[11:0]), .b(12'h1), .out(adder_1_out));  // open: cin, cout
  Adder_16 u_INC (
    .A({4'b0000, Bus_OUT[11:0]}), .B(16'h1), .Cin(1'b0), .S({{3{INC_s[15]}}, INC_s[12:0]}));  // open: Cout
  Register #(.width(12)) PC (.D(multiplexer_1_out), .en(or_1_out), .Q(Bus_OUT[11:0]), .clk(Clock), .clr(Clear));

  assign Bus_OUT[15:12] = 4'b0000;
endmodule

module PC_Controler (
  input  [7:0] D,
  input  [15:0] DR,
  input  [15:0] AC,
  input  [11:0] B,
  input  R,
  input  FGI,
  input  FGO,
  input  E,
  input  r_2,
  input  p,
  input  [15:0] T,
  output Load,
  output Clear,
  output INC
);

  wire and_1_out, and_2_out, and_3_out, and_4_out, and_5_out, and_6_out, and_7_out, and_8_out, and_9_out,
       or_1_out, or_2_out;

  or or_1 (or_1_out, DR[15], DR[14], DR[13], DR[12], DR[11], DR[10], DR[9], DR[8], DR[7], DR[6], DR[5], DR[4], DR[3], DR[2], DR[1], DR[0]);
  or or_2 (or_2_out, AC[15], AC[14], AC[13], AC[12], AC[11], AC[10], AC[9], AC[8], AC[7], AC[6], AC[5], AC[4], AC[3], AC[2], AC[1], AC[0]);
  and and_1 (and_1_out, B[4], r_2, ~AC[15]);  // AND_Gate
  and and_2 (and_2_out, B[3], r_2, AC[15]);
  and and_3 (and_3_out, D[6], T[6], ~or_1_out);  // AND_Gate
  and and_4 (and_4_out, r_2, B[1], ~E);  // AND_Gate
  and and_5 (and_5_out, ~R, T[1]);  // AND_Gate
  and and_6 (and_6_out, R, T[2]);
  and and_7 (and_7_out, B[2], r_2, ~or_2_out);  // AND_Gate
  and and_8 (and_8_out, p, B[9], ~FGI);  // AND_Gate
  and and_9 (and_9_out, p, B[8], FGO);
  and and_10 (Load, D[4], T[4]);
  and and_11 (Clear, R, T[1]);
  or or_3 (INC, and_5_out, and_6_out, and_7_out, and_1_out, and_2_out, and_3_out, and_4_out, and_8_out, and_9_out);

  // Other names for the same wires on the sheet: r_t = r_2
endmodule

module TR (
  input  [15:0] Bus_IN,
  input  [15:0] T,
  input  R,
  input  Clock,
  output [15:0] Bus_OUT
);

  wire and_1_out;

  and and_1 (and_1_out, T[0], R);
  Register #(.width(16)) TR (.D(Bus_IN), .en(and_1_out), .Q(Bus_OUT), .clk(Clock));  // open: clr
endmodule

module DR (
  input  [7:0] D,
  input  [15:0] T,
  input  [15:0] Bus_IN,
  input  Clock,
  output [15:0] Bus_OUT
);

  wire and_1_out, and_2_out, or_1_out, or_2_out;
  wire [15:0] INC_s, multiplexer_1_out;

  or or_1 (or_1_out, D[0], D[1], D[2], D[6]);
  and and_1 (and_1_out, T[4], or_1_out);
  and and_2 (and_2_out, D[6], T[5]);
  Multiplexer #(.width(16), .enable("false")) multiplexer_1 (
    .in0(INC_s), .in1(Bus_IN), .out(multiplexer_1_out), .sel(and_1_out));
  or or_2 (or_2_out, and_1_out, and_2_out);
  Adder_16 INC (.A(Bus_OUT), .B(16'h1), .Cin(1'b0), .S(INC_s));  // open: Cout
  Register #(.width(16)) DR (.D(multiplexer_1_out), .en(or_2_out), .Q(Bus_OUT), .clk(Clock));  // open: clr
endmodule

module OUTR (
  input  [15:0] Bus_IN,
  input  P,
  input  [11:0] B,
  input  Clock,
  output [3:0] out_5,
  output [3:0] out_6
);

  wire and_1_out;

  and and_1 (and_1_out, P, B[10]);
  Register OUTR (.D(Bus_IN[7:0]), .en(and_1_out), .Q({out_6, out_5}), .clk(Clock));  // open: clr
endmodule

module E (
  input  Clock,
  input  r,
  input  [11:0] B,
  input  [7:0] D,
  input  IN,
  input  [15:0] T,
  output E_Out
);

  wire and_1_out, and_2_out, and_3_out, and_4_out, and_5_out, and_6_out, Comp, or_1_out, or_2_out;

  and and_1 (and_1_out, r, B[7]);
  and and_2 (and_2_out, r, B[6]);
  and and_3 (and_3_out, D[1], T[5]);
  or or_1 (or_1_out, and_1_out, and_2_out, and_3_out);
  and and_4 (and_4_out, r, B[8], Comp);
  and and_5 (and_5_out, or_1_out, IN);
  or or_2 (or_2_out, and_4_out, and_5_out);
  D_Flip_Flop E (.clk(Clock), .D(or_2_out), .Q(E_Out), .Qn(Comp), .reset(and_6_out));  // open: preset, en
  and and_6 (and_6_out, r, B[10]);
endmodule

module IEN (
  input  R,
  input  p,
  input  [11:0] B,
  input  Clock,
  input  [15:0] T,
  output OUT
);

  wire and_1_out, and_2_out, and_3_out, or_1_out;

  and and_1 (and_1_out, p, B[7]);
  and and_2 (and_2_out, R, T[2]);
  D_Flip_Flop IEN (.clk(Clock), .D(and_1_out), .Q(OUT), .en(and_1_out), .reset(or_1_out));  // open: Qn, preset
  or or_1 (or_1_out, and_2_out, and_3_out);
  and and_3 (and_3_out, p, B[6]);
endmodule

module FGI (
  input  p,
  input  [11:0] B,
  input  Clock,
  output OUT
);

  wire and_1_out;

  D_Flip_Flop FGI (.clk(Clock), .Q(OUT), .reset(and_1_out));  // open: D, Qn, preset, en
  and and_1 (and_1_out, p, B[11]);
endmodule

module FGO (
  input  p,
  input  [11:0] B,
  input  Clock,
  output OUT
);

  wire and_1_out;

  D_Flip_Flop FGI (.clk(Clock), .Q(OUT), .reset(and_1_out));  // open: D, Qn, preset, en
  and and_1 (and_1_out, p, B[10]);
endmodule

module R (
  input  IEN,
  input  FGO,
  input  FGI,
  input  Clock,
  input  [15:0] T,
  output OUT
);

  wire and_1_out, and_2_out, and_3_out, or_1_out, or_2_out, or_3_out;

  and and_1 (and_1_out, ~T[0], ~T[1], ~T[2]);  // AND_Gate
  or or_1 (or_1_out, FGO, FGI);
  and and_2 (and_2_out, IEN, or_1_out, and_1_out);
  and and_3 (and_3_out, T[2], OUT);
  or or_2 (or_2_out, and_2_out, ~and_3_out);  // OR_Gate
  or or_3 (or_3_out, and_2_out, and_3_out);
  D_Flip_Flop R (.clk(Clock), .D(or_2_out), .Q(OUT), .en(or_3_out));  // open: Qn, preset, reset
endmodule

module AC (
  input  r,
  input  [11:0] B,
  input  [15:0] ALU_IN,
  input  Clock,
  output [15:0] Bus_OUT
);

  wire and_1_out, and_2_out, not_1_out;
  wire [15:0] INC_s, multiplexer_1_out;

  and and_1 (and_1_out, r, B[5]);
  Multiplexer #(.width(16), .enable("false")) multiplexer_1 (
    .in0(INC_s), .in1(ALU_IN), .out(multiplexer_1_out), .sel(not_1_out));
  not not_1 (not_1_out, and_1_out);
  Adder_16 INC (.A(Bus_OUT), .B(16'h1), .Cin(1'b0), .S(INC_s));  // open: Cout
  and and_2 (and_2_out, r, B[11]);
  Register #(.width(16)) AC (.D(multiplexer_1_out), .Q(Bus_OUT), .clk(Clock), .clr(and_2_out));  // open: en
endmodule

module ALU (
  input  [15:0] T,
  input  [7:0] D,
  input  [15:0] AC,
  input  [15:0] DR,
  input  [7:0] INPR,
  input  [11:0] B,
  input  r,
  input  E,
  input  p,
  output [15:0] OUT,
  output E_OUT
);

  wire ADD_out, and_3_out, and_4_out, and_5_out, AND_out, COM_out, Cout, DR_out, INPR_out, not_1_out,
       or_1_out, SHL_out, SHR_out;
  wire [2:0] Selector;
  wire [15:0] adder_1_out, and_2_out, not_2_out;

  and AND (AND_out, D[0], T[5]);
  and ADD (ADD_out, D[1], T[5]);
  and u_DR (DR_out, D[2], T[5]);
  and u_INPR (INPR_out, p, B[11]);
  and COM (COM_out, r, B[9]);
  and SHR (SHR_out, r, B[7]);
  and SHL (SHL_out, r, B[6]);
  or or_1 (or_1_out, SHL_out, SHR_out, COM_out, INPR_out, DR_out, ADD_out, AND_out);
  not not_1 (not_1_out, or_1_out);
  Priority_Encoder priority_encoder_1 (
    .in0(not_1_out), .in1(AND_out), .in2(ADD_out), .in3(DR_out), .in4(INPR_out), .in5(COM_out),
    .in6(SHR_out), .in7(SHL_out), .out(Selector));  // open: en_in, gs, en_out
  assign not_2_out = ~AC;  // NOT_Gate not_2, 16 bits wide
  Adder #(.width(16)) adder_1 (.a(DR), .b(AC), .out(adder_1_out), .cout(Cout));  // open: cin
  assign and_2_out = DR & AC;  // AND_Gate and_2, 16 bits wide
  and and_3 (and_3_out, Cout, ~Selector[0], Selector[1], Selector[2]);  // AND_Gate
  and and_4 (and_4_out, AC[0], ~Selector[0], ~Selector[1], Selector[2]);  // AND_Gate
  and and_5 (and_5_out, AC[15], Selector[0], Selector[1], ~Selector[2]);  // AND_Gate
  or or_2 (E_OUT, and_3_out, and_4_out, and_5_out);
  Multiplexer #(.select(3), .width(16), .enable("false")) multiplexer_1 (
    .in0(AC), .in1(and_2_out), .in2(adder_1_out), .in3(DR), .in4({{8{1'b0}}, INPR}), .in5(not_2_out),
    .in6({E, AC[15:1]}), .in7({AC[14:0], E}), .out(OUT), .sel(Selector));
endmodule

module SC (
  input  [15:0] T,
  input  R,
  input  Clock,
  input  [7:0] D,
  input  I,
  output [15:0] T_2
);

  wire and_1_out, and_2_out, and_3_out, and_4_out, and_5_out, and_6_out, and_7_out, and_8_out, D4_out,
       or_1_out, or_2_out, T4_out, T6_out;
  wire [3:0] register_1_q;
  wire [15:0] adder_16_1_s;

  and and_1 (and_1_out, D[2], T[6]);
  and and_2 (and_2_out, D[1], T[6]);
  and T4 (T4_out, D[3], T[5]);
  and D4 (D4_out, D[4], T[5]);
  and and_3 (and_3_out, D[0], T[6]);
  and and_4 (and_4_out, D[5], T[6]);
  and and_5 (and_5_out, R, T[3]);
  and T6 (T6_out, D[6], T[7]);
  and and_6 (and_6_out, D[7], ~D[7], T[4]);  // AND_Gate
  and and_7 (and_7_out, D[7], D[7], T[4]);
  Adder_16 adder_16_1 (.A({{12{1'b0}}, register_1_q}), .B(16'h1), .Cin(1'b0), .S(adder_16_1_s));  // open: Cout
  or or_1 (or_1_out, and_5_out, and_3_out, and_2_out, and_1_out, T4_out, D4_out, and_4_out, T6_out, and_6_out, and_7_out);
  Register #(.width(4)) register_1 (.D(adder_16_1_s[3:0]), .Q(register_1_q), .clk(Clock), .clr(or_2_out));  // open: en
  or or_2 (or_2_out, or_1_out, and_8_out);
  and and_8 (and_8_out, register_1_q[3], register_1_q[2], register_1_q[1], register_1_q[0]);
  Decoder #(.select(4)) decoder_1 (
    .out0(T_2[0]), .out1(T_2[1]), .out2(T_2[2]), .out3(T_2[3]), .out4(T_2[4]), .out5(T_2[5]), .out6(T_2[6]),
    .out7(T_2[7]), .out8(T_2[8]), .out9(T_2[9]), .out10(T_2[10]), .out11(T_2[11]), .out12(T_2[12]),
    .out13(T_2[13]), .out14(T_2[14]), .out15(T_2[15]), .sel(register_1_q));  // open: en

  assign I = D[7];
endmodule

module BUS_Controler (
  input  [15:0] T,
  input  [7:0] D,
  input  R,
  input  p,
  input  I,
  input  [11:0] B,
  output [2:0] BUS
);

  wire AC_out, and_1_out, and_2_out, and_3_out, and_4_out, and_5_out, and_6_out, and_7_out, and_8_out,
       and_9_out, and_10_out, AR_out, DR_out, IR_out, MR_out, or_1_out, PC_out, TR_out;

  and and_1 (and_1_out, p, B[10]);
  and and_2 (and_2_out, D[5], T[5]);
  and and_3 (and_3_out, D[2], T[5]);
  and and_4 (and_4_out, ~R, T[1]);  // AND_Gate
  or or_1 (or_1_out, D[0], D[1], D[2], D[6]);
  or PC (PC_out, T[0], and_5_out);
  and and_5 (and_5_out, D[5], T[4]);
  and TR (TR_out, R, T[1]);
  and IR (IR_out, ~R, T[2]);  // AND_Gate
  and and_6 (and_6_out, D[3], T[4]);
  or AC (AC_out, and_6_out, and_1_out);
  and and_7 (and_7_out, D[4], T[4]);
  or AR (AR_out, and_7_out, and_2_out);
  and and_8 (and_8_out, D[6], T[6]);
  or DR (DR_out, and_8_out, and_3_out);
  and and_9 (and_9_out, ~D[7], I, T[3]);  // AND_Gate
  and and_10 (and_10_out, T[4], or_1_out);
  or MR (MR_out, and_9_out, and_4_out, and_10_out);
  Priority_Encoder priority_encoder_1 (
    .in1(PC_out), .in2(TR_out), .in3(IR_out), .in4(AC_out), .in5(AR_out), .in6(DR_out), .in7(MR_out),
    .out(BUS));  // open: in0, en_in, gs, en_out
endmodule

module MR_Controler (
  input  [15:0] T,
  input  [7:0] D,
  input  R,
  output MR_LD
);

  wire and_1_out, and_2_out, and_3_out, and_4_out, or_1_out;

  and and_1 (and_1_out, R, T[1]);
  and and_2 (and_2_out, D[3], T[4]);
  and and_3 (and_3_out, D[6], T[6]);
  and and_4 (and_4_out, D[5], T[4]);
  or or_1 (or_1_out, and_1_out, and_2_out, and_3_out, and_4_out);
  not not_1 (MR_LD, or_1_out);
endmodule
